# Fritzing sketch DCC-Encoder-Throttle (saved by Fritzing 0.9.3b)
circuit board: 7.5cm x 6.1cm
breadboards: 1

parts:
  RE1 = Rotary Encoder [package=THT]
  J1 = female pin header, 2 pins [form="♀ (female)"]
  J2 = female pin header, 4 pins [form="♀ (female)"]
  Nano = Arduino Nano (Rev3.0)
  R1 = Resistor [tolerance=±5% power=0.25 resistance=10k package=THT]
  J3 = female pin header, 10 pins [form="♀ (female)"]
  J4 = female pin header, 4 pins [form="♀ (female)"]

nets:
  N1: RE1.EncoderPinA, Nano.D2
  N2: RE1.EncoderPinB, Nano.D3
  N3: J1.pin2, Nano.D4, R1.Pin_0
  N4: J2.pin1, Nano.A5
  N5: J2.pin2, Nano.A4
  N6: J2.pin3, Nano.5V, R1.Pin_1, J4.pin1
  N7: J2.pin4, Nano.GND, J4.pin2
  N8: Nano.D1/TX, J4.pin3
  N9: Nano.D0/RX, J4.pin4
  N10: Nano.D5, J3.pin1
  N11: Nano.D6, J3.pin2
  N12: Nano.D7, J3.pin3
  N13: Nano.D8, J3.pin4
  N14: Nano.D9, J3.pin5
  N15: Nano.D10, J3.pin6
  N16: Nano.D11/MOSI, J3.pin7
  N17: Nano.D12/MISO, J3.pin8

notes:
  +
  -
  RX
  TX
